# Fritzing sketch servo-wiring (saved by Fritzing 0.8.7b)
breadboards: 1

parts:
  Part1 = Arduino Uno (Rev3)
  Standard-sized_Servo = Basic Servo
  VCC1 = 4 x AAA Battery Mount
  Sub-micro-sized_Servo = Basic Servo

nets:
  N1: Part1.D9_PWM, Standard-sized_Servo.pulse
  N2: Part1.D10_PWM/SS, Sub-micro-sized_Servo.pulse
  GND: Part1.GND, Standard-sized_Servo.gnd, VCC1.-, Sub-micro-sized_Servo.gnd
  N3: Standard-sized_Servo.vcc, VCC1.+

notes:
  Make sure you wire the sub-micro server with plenty of wire slack: about 8 inches ideally
