# Fritzing sketch sundial-wiring (saved by Fritzing 0.8.7b)
breadboards: 1

parts:
  Part1 = Arduino Uno (Rev3)
  Standard-sized_Servo = Basic Servo
  VCC1 = 4 x AAA Battery Mount
  Sub-micro-sized_Servo = Basic Servo
  LED1 = LED - 5mm [color="White (4500K)" package="5 mm [THT]"]
  R1 = Resistor [tolerance=±5% resistance=220 package=THT]

nets:
  N1: Part1.D9_PWM, Standard-sized_Servo.pulse
  N2: Part1.D10_PWM/SS, Sub-micro-sized_Servo.pulse
  5V: Part1.5V, Sub-micro-sized_Servo.vcc, LED1.anode
  GND: Part1.GND, Standard-sized_Servo.gnd, VCC1.-, Sub-micro-sized_Servo.gnd, R1.Pin_1
  N3: Standard-sized_Servo.vcc, VCC1.+
  N4: LED1.cathode, R1.Pin_0

notes:
  Make sure you wire the sub-micro server with plenty of wire slack: about 8 inches ideally
  LED wires should be about 16" long.
