# Fritzing sketch cheerfulj5-uno (saved by Fritzing 0.8.7b)
breadboards: 1

parts:
  R1 = Resistor [tolerance=±5% resistance=270 package=THT]
  R2 = Resistor [tolerance=±5% resistance=270 package=THT]
  R3 = Resistor [tolerance=±5% resistance=270 package=THT]
  LED1 = RGB LED (com. cathode, rbg) [package="5 mm [THT]"]
  Part1 = Arduino Uno (Rev3)

nets:
  N1: R1.Pin_0, LED1.blue_anode
  N2: R1.Pin_1, Part1.D5_PWM
  N3: R2.Pin_0, LED1.red_anode
  N4: R2.Pin_1, Part1.D3_PWM
  N5: R3.Pin_0, LED1.green_anode
  N6: R3.Pin_1, Part1.D6_PWM
  N7: LED1.common_cathode, Part1.GND
