# Fritzing sketch simplebot_sonic (saved by Fritzing 0.9.0b)
breadboards: 1

parts:
  7_4V_Pack = LIPO-1000mAh [package=lipo-1000]
  J1 = Basic Servo
  J2 = Basic Servo
  Part1 = Arduino Nano (Rev3.0)
  IC1 = Voltage Regulator [package=to-220-alt]
  Part2 = SRF05

nets:
  N1: 7_4V_Pack.+, IC1.GND
  GND: 7_4V_Pack.-, J1.gnd, J2.gnd, Part1.GND, IC1.IN, Part2.GND
  VCC: J1.vcc, J2.vcc, IC1.OUT
  N2: J1.pulse, Part1.D9
  N3: J2.pulse, Part1.D8
  N4: Part1.D7, Part2.Trig, Part2.Echo
  5V: Part1.5V, Part2.VCC

custom parts:
  LIPO-1000mAh: 1000mAh Lipo-battery
