# Fritzing sketch simplebot_wireless (saved by Fritzing 0.9.0b)
breadboards: 1

parts:
  7_4V_Pack = LIPO-1000mAh [package=lipo-1000]
  J1 = Basic Servo
  J2 = Basic Servo
  Part1 = Arduino Nano (Rev3.0)
  IC1 = Voltage Regulator [package=to-220-alt]
  WiFi232-T = Header 10 [package=1x10-2mm-smd]
  C2 = Capacitor [package=cap-pth-small-kit]
  C3 = Capacitor [package=cap-pth-small-kit]
  C4 = Capacitor [package=cap-pth-small]

nets:
  VIN: 7_4V_Pack.+, Part1.VIN, IC1.GND, C2.2
  GND: 7_4V_Pack.-, J1.gnd, J2.gnd, Part1.GND, IC1.IN, WiFi232-T.1, C2.1, C3.1, C4.2
  VCC: J1.vcc, J2.vcc, IC1.OUT, C3.2, C4.1
  N1: J1.pulse, Part1.D9
  N2: J2.pulse, Part1.D8
  N3: Part1.D1/TX, WiFi232-T.5
  N4: Part1.D0/RX, WiFi232-T.6
  N5: Part1.3V3, WiFi232-T.2

custom parts:
  LIPO-1000mAh: 1000mAh Lipo-battery
